// Logisim project entradaL5.circ as structural Verilog: 1 circuit, main circuit main
module main (
  input  A,
  input  B,
  input  C,
  input  D,
  input  E,
  output L5
);

  wire nand_1_out, nand_2_out, nand_3_out, nand_4_out, nand_5_out, nand_6_out, nand_7_out, nand_8_out,
       nand_9_out, nand_10_out;

  nand nand_1 (nand_1_out, B, B);
  nand nand_2 (nand_2_out, B, B);
  nand nand_3 (nand_3_out, C, C);
  nand nand_4 (nand_4_out, D, D);
  nand nand_5 (nand_5_out, C, C);
  nand nand_6 (nand_6_out, E, E);
  nand nand_7 (nand_7_out, A, nand_1_out, C, E);
  nand nand_8 (nand_8_out, A, nand_2_out, C, D);
  nand nand_9 (nand_9_out, A, B, nand_3_out, nand_4_out);
  nand nand_10 (nand_10_out, A, B, nand_5_out, nand_6_out);
  nand nand_11 (L5, nand_7_out, nand_8_out, nand_9_out, nand_10_out);
endmodule
